// Logisim project lab-5_q.circ as structural Verilog: 2 circuits, main circuit main
module main (
  input  in_1,
  input  in_2,
  input  in_3,
  input  in_4,
  input  in_5,
  output out_6,
  output out_7
);

  wire and_1_out, and_2_out, and_3_out, and_4_out, and_5_out, and_6_out, and_7_out, and_8_out, and_9_out,
       and_10_out, and_11_out, and_12_out, and_13_out, and_14_out, clk_2phase_1_phi_1, clk_2phase_1_phi_2,
       nand_1_out, nand_2_out, nand_3_out, nand_4_out, nand_5_out, nand_6_out, nand_7_out, nand_8_out,
       nand_9_out, nand_10_out, nand_11_out, nand_12_out, nand_13_out, nand_14_out, nand_16_out, nand_17_out,
       nand_18_out, nand_19_out, nand_20_out, nand_21_out, nand_22_out, nand_23_out, nand_24_out,
       nand_25_out, nand_26_out, nand_27_out, nand_28_out, nand_29_out, nand_30_out, nand_32_out, not_1_out,
       not_2_out, not_3_out, not_4_out, not_5_out, or_1_out, or_2_out, xor_1_out, xor_2_out, xor_3_out,
       xor_4_out;

  not not_1 (not_1_out, in_1);
  clk_2phase clk_2phase_1 (.phi_1(clk_2phase_1_phi_1), .phi_2(clk_2phase_1_phi_2));
  not not_2 (not_2_out, and_7_out);
  not not_3 (not_3_out, nand_13_out);
  and and_1 (and_1_out, in_4, out_6);
  and and_2 (and_2_out, and_7_out, clk_2phase_1_phi_2);
  and and_3 (and_3_out, clk_2phase_1_phi_2, not_2_out);
  xor xor_1 (xor_1_out, out_6, in_4);
  or or_1 (or_1_out, and_1_out, and_6_out);
  and and_4 (and_4_out, nand_13_out, clk_2phase_1_phi_1);
  and and_5 (and_5_out, clk_2phase_1_phi_1, not_3_out);
  and and_6 (and_6_out, in_2, xor_1_out);
  nand nand_1 (nand_1_out, and_2_out, and_2_out);
  nand nand_2 (nand_2_out, nand_14_out, nand_14_out);
  nand nand_3 (nand_3_out, nand_13_out, nand_13_out);
  nand nand_4 (nand_4_out, and_3_out, and_3_out);
  nand nand_5 (nand_5_out, and_4_out, and_4_out);
  nand nand_6 (nand_6_out, nand_16_out, nand_16_out);
  nand nand_7 (nand_7_out, out_6, out_6);
  nand nand_8 (nand_8_out, and_5_out, and_5_out);
  nand nand_9 (nand_9_out, nand_1_out, nand_2_out);
  nand nand_10 (nand_10_out, nand_3_out, nand_4_out);
  xor xor_2 (xor_2_out, in_2, xor_1_out);
  and and_7 (and_7_out, not_1_out, xor_2_out);
  nand nand_11 (nand_11_out, nand_5_out, nand_6_out);
  nand nand_12 (nand_12_out, nand_7_out, nand_8_out);
  nand nand_13 (nand_13_out, nand_9_out, nand_9_out);
  nand nand_14 (nand_14_out, nand_10_out, nand_10_out);
  nand nand_15 (out_6, nand_11_out, nand_11_out);
  nand nand_16 (nand_16_out, nand_12_out, nand_12_out);
  not not_4 (not_4_out, and_14_out);
  not not_5 (not_5_out, nand_29_out);
  and and_8 (and_8_out, in_5, out_7);
  and and_9 (and_9_out, and_14_out, clk_2phase_1_phi_2);
  and and_10 (and_10_out, clk_2phase_1_phi_2, not_4_out);
  xor xor_3 (xor_3_out, out_7, in_5);
  or or_2 (or_2_out, and_8_out, and_13_out);
  and and_11 (and_11_out, nand_29_out, clk_2phase_1_phi_1);
  and and_12 (and_12_out, clk_2phase_1_phi_1, not_5_out);
  and and_13 (and_13_out, in_3, xor_3_out);
  nand nand_17 (nand_17_out, and_9_out, and_9_out);
  nand nand_18 (nand_18_out, nand_30_out, nand_30_out);
  nand nand_19 (nand_19_out, nand_29_out, nand_29_out);
  nand nand_20 (nand_20_out, and_10_out, and_10_out);
  xor xor_4 (xor_4_out, in_3, xor_3_out);
  nand nand_21 (nand_21_out, and_11_out, and_11_out);
  nand nand_22 (nand_22_out, nand_32_out, nand_32_out);
  nand nand_23 (nand_23_out, out_7, out_7);
  nand nand_24 (nand_24_out, and_12_out, and_12_out);
  nand nand_25 (nand_25_out, nand_17_out, nand_18_out);
  nand nand_26 (nand_26_out, nand_19_out, nand_20_out);
  and and_14 (and_14_out, not_1_out, xor_4_out);
  nand nand_27 (nand_27_out, nand_21_out, nand_22_out);
  nand nand_28 (nand_28_out, nand_23_out, nand_24_out);
  nand nand_29 (nand_29_out, nand_25_out, nand_25_out);
  nand nand_30 (nand_30_out, nand_26_out, nand_26_out);
  nand nand_31 (out_7, nand_27_out, nand_27_out);
  nand nand_32 (nand_32_out, nand_28_out, nand_28_out);
endmodule

module clk_2phase (
  output phi_1,
  output phi_2
);

  wire clock_1_out, nand_1_out, nand_2_out, not_1_out, not_2_out, not_3_out;

  Clock clock_1 (.out(clock_1_out));
  not not_1 (not_1_out, clock_1_out);
  nand nand_1 (nand_1_out, not_1_out, phi_2);
  not not_2 (not_2_out, nand_1_out);
  nand nand_2 (nand_2_out, phi_1, clock_1_out);
  not not_3 (not_3_out, nand_2_out);
  not not_4 (phi_1, not_2_out);
  not not_5 (phi_2, not_3_out);
endmodule
