// Logisim project n-bit_counter.circ as structural Verilog: 2 circuits, main circuit clk_2phase
module main (
  input  in_1,
  input  in_2,
  input  in_3,
  input  in_4,
  input  in_5,
  output out_6,
  output out_7,
  output out_8
);

  wire adder_1_cout, adder_1_out, adder_2_cout, adder_2_out, adder_3_cout, adder_3_out, and_1_out, and_2_out,
       and_3_out, clk_2phase_1_phi_1, clk_2phase_1_phi_2, d_ff_1_q, d_ff_3_q, d_ff_5_q, not_1_out;

  clk_2phase clk_2phase_1 (.phi_2(clk_2phase_1_phi_2), .phi_1(clk_2phase_1_phi_1));
  not not_1 (not_1_out, in_1);
  D_Flip_Flop d_ff_1 (.clk(clk_2phase_1_phi_2), .D(and_1_out), .Q(d_ff_1_q));  // open: Qn, preset, en, reset
  and and_1 (and_1_out, not_1_out, adder_1_out);
  Adder #(.width(1)) adder_1 (.a(out_6), .b(in_3), .out(adder_1_out), .cin(in_2), .cout(adder_1_cout));
  D_Flip_Flop d_ff_2 (.clk(clk_2phase_1_phi_1), .D(d_ff_1_q), .Q(out_6));  // open: Qn, preset, en, reset
  D_Flip_Flop d_ff_3 (.clk(clk_2phase_1_phi_2), .D(and_2_out), .Q(d_ff_3_q));  // open: Qn, preset, en, reset
  and and_2 (and_2_out, not_1_out, adder_2_out);
  Adder #(.width(1)) adder_2 (.a(out_7), .b(in_4), .out(adder_2_out), .cin(adder_1_cout), .cout(adder_2_cout));
  D_Flip_Flop d_ff_4 (.clk(clk_2phase_1_phi_1), .D(d_ff_3_q), .Q(out_7));  // open: Qn, preset, en, reset
  D_Flip_Flop d_ff_5 (.clk(clk_2phase_1_phi_2), .D(and_3_out), .Q(d_ff_5_q));  // open: Qn, preset, en, reset
  and and_3 (and_3_out, not_1_out, adder_3_out);
  Adder #(.width(1)) adder_3 (.a(out_8), .b(in_5), .out(adder_3_out), .cin(adder_2_cout), .cout(adder_3_cout));
  D_Flip_Flop d_ff_6 (.clk(clk_2phase_1_phi_1), .D(d_ff_5_q), .Q(out_8));  // open: Qn, preset, en, reset
endmodule

// CLK
module clk_2phase (
  output phi_2,
  output phi_1
);

  wire clock_1_out, nand_1_out, nand_2_out, not_1_out, not_2_out, not_3_out;

  Clock clock_1 (.out(clock_1_out));
  not not_1 (not_1_out, clock_1_out);
  nand nand_1 (nand_1_out, not_1_out, phi_1);
  not not_2 (not_2_out, nand_1_out);
  nand nand_2 (nand_2_out, phi_2, clock_1_out);
  not not_3 (not_3_out, nand_2_out);
  not not_4 (phi_2, not_2_out);
  not not_5 (phi_1, not_3_out);
endmodule
