// Logisim project streetlight.circ as structural Verilog: 2 circuits, main circuit clk_2phase
module main (
  input  in_1,
  input  in_2,
  input  in_3,
  input  in_4,
  input  in_5,
  output out_6
);

  wire adder_1_cout, adder_1_out, adder_2_cout, adder_2_out, adder_3_cout, adder_3_out, and_1_out, and_2_out,
       and_3_out, and_4_out, and_5_out, and_6_out, and_7_out, and_8_out, and_9_out, and_10_out, and_11_out,
       and_12_out, button_1_out, clk_2phase_1_phi_1, clk_2phase_1_phi_2, d_ff_1_q, d_ff_2_q, d_ff_3_q,
       d_ff_4_q, d_ff_5_q, d_ff_6_q, not_1_out, not_2_out, not_3_out, not_4_out, not_5_out, not_6_out,
       not_7_out, not_8_out, not_9_out, not_10_out, not_11_out, not_12_out, not_13_out, or_1_out, or_2_out,
       or_3_out;

  clk_2phase clk_2phase_1 (.phi_2(clk_2phase_1_phi_2), .phi_1(clk_2phase_1_phi_1));
  not not_1 (not_1_out, in_1);
  Button button_1 (.out(button_1_out));
  D_Flip_Flop d_ff_1 (.clk(clk_2phase_1_phi_2), .D(and_1_out), .Q(d_ff_1_q));  // open: Qn, preset, en, reset
  and and_1 (and_1_out, not_1_out, adder_1_out);
  Adder #(.width(1)) adder_1 (.a(d_ff_2_q), .b(in_3), .out(adder_1_out), .cin(in_2), .cout(adder_1_cout));
  D_Flip_Flop d_ff_2 (.clk(clk_2phase_1_phi_1), .D(d_ff_1_q), .Q(d_ff_2_q));  // open: Qn, preset, en, reset
  not not_2 (not_2_out, d_ff_4_q);
  and and_2 (and_2_out, d_ff_2_q, not_2_out);
  and and_3 (and_3_out, d_ff_4_q, d_ff_6_q);
  or or_1 (or_1_out, and_3_out, and_2_out, and_4_out);
  not not_3 (not_3_out, d_ff_4_q);
  not not_4 (not_4_out, d_ff_6_q);
  not not_5 (not_5_out, d_ff_2_q);
  not not_6 (not_6_out, d_ff_4_q);
  and and_4 (and_4_out, not_6_out, not_4_out);
  and and_5 (and_5_out, not_5_out, not_3_out, d_ff_6_q);
  or or_2 (or_2_out, and_5_out, and_7_out);
  D_Flip_Flop d_ff_3 (.clk(clk_2phase_1_phi_2), .D(and_6_out), .Q(d_ff_3_q));  // open: Qn, preset, en, reset
  and and_6 (and_6_out, not_1_out, adder_2_out);
  Adder #(.width(1)) adder_2 (.a(d_ff_4_q), .b(in_4), .out(adder_2_out), .cin(adder_1_cout), .cout(adder_2_cout));
  D_Flip_Flop d_ff_4 (.clk(clk_2phase_1_phi_1), .D(d_ff_3_q), .Q(d_ff_4_q));  // open: Qn, preset, en, reset
  not not_7 (not_7_out, d_ff_2_q);
  not not_8 (not_8_out, d_ff_2_q);
  not not_9 (not_9_out, d_ff_6_q);
  and and_7 (and_7_out, not_8_out, d_ff_4_q, not_9_out);
  and and_8 (and_8_out, d_ff_2_q, d_ff_4_q);
  or or_3 (or_3_out, d_ff_4_q, and_10_out);
  not not_10 (not_10_out, d_ff_4_q);
  not not_11 (not_11_out, d_ff_2_q);
  and and_9 (and_9_out, d_ff_2_q, not_10_out);
  and and_10 (and_10_out, not_7_out, d_ff_6_q);
  D_Flip_Flop d_ff_5 (.clk(clk_2phase_1_phi_2), .D(and_11_out), .Q(d_ff_5_q));  // open: Qn, preset, en, reset
  and and_11 (and_11_out, not_1_out, adder_3_out);
  Adder #(.width(1)) adder_3 (.a(d_ff_6_q), .b(in_5), .out(adder_3_out), .cin(adder_2_cout), .cout(adder_3_cout));
  D_Flip_Flop d_ff_6 (.clk(clk_2phase_1_phi_1), .D(d_ff_5_q), .Q(d_ff_6_q));  // open: Qn, preset, en, reset
  not not_12 (not_12_out, d_ff_4_q);
  not not_13 (not_13_out, d_ff_6_q);
  and and_12 (and_12_out, not_11_out, not_12_out, not_13_out);
  LED led_1 (.in(or_3_out));
  LED led_2 (.in(and_9_out));
  LED led_3 (.in(and_12_out));
  LED led_4 (.in(or_1_out));
  LED led_5 (.in(or_2_out));
  LED led_6 (.in(and_8_out));

  // Notes on the sheet:
  //   RST
  //   Q0
  //   Q1
  //   Q2
  //   MAIN ST
  //   ACCESS ST
endmodule

// CLK
module clk_2phase (
  output phi_2,
  output phi_1
);

  wire clock_1_out, nand_1_out, nand_2_out, not_1_out, not_2_out, not_3_out;

  Clock clock_1 (.out(clock_1_out));
  not not_1 (not_1_out, clock_1_out);
  nand nand_1 (nand_1_out, not_1_out, phi_1);
  not not_2 (not_2_out, nand_1_out);
  nand nand_2 (nand_2_out, phi_2, clock_1_out);
  not not_3 (not_3_out, nand_2_out);
  not not_4 (phi_2, not_2_out);
  not not_5 (phi_1, not_3_out);
endmodule
